# Fritzing sketch MR-990 (saved by Fritzing 1.0.3b)
breadboards: 1

parts:
  Teensy2 = Teensy 4.1
  A1 = Pcm5102A module
  A2 = Pcm5102A module

nets:
  N1: Teensy2.GND, Teensy2.GND2#55, A1.Pin_1, A1.Pin_5, A2.Pin_1, A2.Pin_5
  N2: Teensy2.D7, A1.Pin_3
  N3: Teensy2.A6/D20, Teensy2.D32, A1.Pin_4, A2.Pin_3
  N4: Teensy2.A7/D21, A1.Pin_2, A2.Pin_2
  N5: Teensy2.Vin, A1.Pin_6, A2.Pin_6

custom parts:
  Teensy 4.1: The Teensy is a complete USB-based microcontoller development system, in a very small footprint, capable of implementing many types of projects. All programming is done via the USB port. No special programmer is needed, only a standard micro-USB cable and a PC or Macintosh with a USB port.
  Pcm5102A module: Interface I2S PCM5102A DAC Decoder GY-PCM5102 I2S Player Module for Raspberry Pi pHAT Format Board Digital PCM5102 Audio Board.
